# Fritzing sketch cloudy_hardware8 (saved by Fritzing 0.9.10b)

parts:
  M1 = >Wemos D1 R32
  Mod1 = Raspberry Pi 4B
  Part3 = NeoPixel Stick [part_number=1426]
  Part4 = Adafruit TCA9548A
  J18 = XT30 Connector male [package=THT]
  F1 = Fan - Ventilador [package=THT]
  Part6 = NeoPixel Stick [part_number=1426]
  Part7 = NeoPixel Stick [part_number=1426]
  Part8 = NeoPixel Stick [part_number=1426]
  OLED_I2C1 = OLED 128x64 I2C Monochrome Display
  Part11 = InvenSense MPU6050
  J56 = JST connector male [package=THT]
  J51 = JST connector female [package=THT]
  J44 = JST connector female [package=THT]
  J46 = push button [package=THT]
  J64 = Intel Realsense D435i [package=THT]  # not connected
  BAT3 = Lion Battery Pack 6s 3200mAh [package=lipo-1100mAh]
  USBTTL1 = USB A Plug  # not connected
  USBTTL2 = Micro USB B Plug
  J6 = IBUS Receiver [package=THT]
  USBTTL3 = USB A Plug
  Arduino_CNC_Shield_V3_00_1 = Arduino_CNC_V3.00
  M7 = Stepper Motor - Bipolar
  M8 = Stepper Motor - Bipolar
  USBTTL5 = USB A Plug  # not connected
  F3 = USB WIFI [package=THT]  # not connected
  J74 = Camdenboss CTB0158-8 [part_number=CTB0158-8 package=THT]
  J75 = Camdenboss CTB0158-8 [part_number=CTB0158-8 package=THT]
  J76 = Camdenboss CTB0158-8 [part_number=CTB0158-8 package=THT]  # not connected
  J77 = Camdenboss CTB0158-8 [part_number=CTB0158-8 package=THT]
  J78 = Camdenboss CTB0158-8 [part_number=CTB0158-8 package=THT]
  J79 = Camdenboss CTB0158-8 [part_number=CTB0158-8 package=THT]  # not connected
  J12 = emergency button [package=THT]
  J80 = Metal Push On-Off Switch [package=THT]
  J81 = DC Jack Barrel [package=THT]
  J82 = DC Jack Barrel [package=THT]
  J87 = Camdenboss CTB0158-8 [part_number=CTB0158-8 package=THT]
  J89 = Camdenboss CTB0158-8 [part_number=CTB0158-8 package=THT]
  J90 = Camdenboss CTB0158-8 [part_number=CTB0158-8 package=THT]
  F2 = RPLIDAR A1M8 [package=THT]  # not connected
  U4 = UBEC 5V6A [package=THT]
  J17 = XT30 Connector female [package=THT]
  J91 = JST connector male [package=THT]
  J92 = JST connector female [package=THT]
  J93 = JST connector male [package=THT]
  J94 = JST connector female [package=THT]
  U5 = Mini-360 DC-DC Buck converter [package=THT]
  J95 = JST connector male [package=THT]
  J96 = JST connector male [package=THT]
  J97 = JST connector female [package=THT]
  J88 = Camdenboss CTB0158-8 [part_number=CTB0158-8 package=THT]
  INA1 = INA219 DC Current Sensor Breakout
  Part16 = Adafruit APDS-9960 [part_number="Adafruit #3595"]
  Part17 = Adafruit APDS-9960 [part_number="Adafruit #3595"]
  Part18 = Adafruit APDS-9960 [part_number="Adafruit #3595"]

nets:
  N1: M1.SCL, J96.pin2
  3V3: Mod1.3V3, Part11.VCC
  N2: Mod1.GPIO2, Part11.SCL
  N3: Mod1.5V, J44.pin1
  N4: Mod1.GPIO3, Part11.SDA
  GND: Mod1.GND, Part11.GND, J44.pin2
  GND_2: Part3.GND, Part6.GND, J88.pin7
  N5: Part3.DATAOUT, Part6.DATAIN
  +5V: Part3.+5V, Part6.+5V, J88.pin8
  N6: Part3.DATAIN, J88.pin5
  N7: Part4.2SDA, J87.pin6
  N8: Part4.2SCL, J87.pin5
  N9: Part4.3SDA, J77.pin7
  N10: Part4.3SCL, J77.pin6
  N11: Part4.4SDA, J78.pin6
  N12: Part4.4SCL, J78.pin5
  N13: Part4.VCC, Arduino_CNC_Shield_V3_00_1.5V#75, J77.pin5, J87.pin1, U5.OUT+
  GND_3: Part4.GND, J18.GND, J77.pin1, J87.pin2, U5.OUT-
  N14: Part4.INPUTSDA, J97.pin1
  N15: Part4.INPUTSCL, J97.pin2
  N16: Part4.0SDA, J90.pin2
  N17: Part4.0SCL, J90.pin1
  N18: Part4.1SDA, J87.pin8
  N19: Part4.1SCL, J87.pin7
  N20: J18.VCC, J77.pin3, INA1.Vin+
  N21: F1.5V, J51.pin1
  N22: F1.GND, J51.pin2
  GND_4: Part7.GND, Part8.GND, OLED_I2C1.GND, J74.pin8
  N23: Part7.DATAOUT, Part8.DATAIN
  +5V_2: Part7.+5V, Part8.+5V, OLED_I2C1.VDD, J74.pin4, INA1.VCC
  N24: Part7.DATAIN, J74.pin1
  N25: Part8.DATAOUT, J75.pin5
  N26: OLED_I2C1.SDA, J74.pin2
  N27: OLED_I2C1.SCK, J74.pin3
  N28: J56.pin1, Arduino_CNC_Shield_V3_00_1.POWER_+, J78.pin3
  N29: J56.pin2, Arduino_CNC_Shield_V3_00_1.POWER_-
  N30: J46.pin2, J75.pin8
  N31: BAT3.+, J17.VCC
  N32: BAT3.-, J17.GND
  N33: USBTTL2.usb, USBTTL3.usb
  GND_5: J6.gnd, Arduino_CNC_Shield_V3_00_1.GND
  N34: J6.Vcc, Arduino_CNC_Shield_V3_00_1.5V#11
  N35: J6.ibus, Arduino_CNC_Shield_V3_00_1.X.DIR
  N36: Arduino_CNC_Shield_V3_00_1.X.STEP, J77.pin8
  N37: Arduino_CNC_Shield_V3_00_1.Z-MTR_'1', M8.A
  N38: Arduino_CNC_Shield_V3_00_1.Z-MTR_'2', M8.C
  N39: Arduino_CNC_Shield_V3_00_1.Z-MTR_'4', M8.D
  N40: Arduino_CNC_Shield_V3_00_1.Y-MTR_'1', M7.A
  N41: Arduino_CNC_Shield_V3_00_1.Y-MTR_'2', M7.C
  N42: Arduino_CNC_Shield_V3_00_1.Y-MTR_'3', M7.B
  N43: Arduino_CNC_Shield_V3_00_1.Y-MTR_'4', M7.D
  N44: Arduino_CNC_Shield_V3_00_1.3V3, J87.pin3
  N45: Arduino_CNC_Shield_V3_00_1.RST, J78.pin1
  N46: J74.pin6, J80.pin2, J81.pin_3, J82.pin_3
  N47: J74.pin7, J80.pin_5, J82.pin1
  N48: J75.pin3, INA1.SDA
  N49: J75.pin4, INA1.SCL
  N50: J75.pin6, J12.pin1
  N51: J77.pin2, J91.pin2, J93.pin2
  N52: J78.pin2, J91.pin1, J93.pin1
  N53: J78.pin4, J87.pin4
  N54: J12.pin2, J80.pin_3, J80.pin_4
  N55: J81.pin1, J81.pin2
  N56: J89.pin7, Part18.SDA
  N57: J89.pin8, Part18.SCL
  N58: U4.IN-, J95.pin2
  N59: U4.IN+, J95.pin1
  N60: U4.OUT+, J92.pin1
  N61: U4.OUT-, J92.pin2
  N62: J94.pin1, U5.IN+
  N63: J94.pin2, U5.IN-
  N64: J88.pin1, Part17.SDA
  N65: J88.pin2, Part17.SCL
  N66: J88.pin3, Part16.SDA
  N67: J88.pin4, Part16.SCL
  VIN: J88.pin6, Part16.VIN, Part17.VIN, Part18.VIN

notes:
  22.2V Li-on Battery 3200 mAh
  UBEC
  5V 6A
  OUT
  IN

custom parts:
  >Wemos D1 R32: Wemos D1 R32 - This board is used with dual-mode Wi-Fi and Bluetooth chips, which is safe, reliable, and scalable to a variety of applications. DC in 5V-12V, 1 analog input(3.2V max input), a Micro USB connection, Compatible with D1 R32=WiFi+bluetooth+UNO
  NeoPixel Stick: Make your own little LED strip arrangement with this stick of NeoPixel LEDs. We crammed 8 of the tiny 5050 (5mm x 5mm) smart RGB LEDs onto a PCB with mounting holes and a chainable design. Use only one microcontroller pin to control as many as you can chain together! Each LED is addressable as the driver chip is inside the LED. Each one has ~18mA constant current drive so the color will be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
  Adafruit TCA9548A: You just found the perfect I2C sensor, and you want to wire up two or three or more of them to your Arduino when you realize "Uh oh, this chip has a fixed I2C address, and from what I know about I2C, you cannot have two devices with the same address on the same SDA/SCL pins!" Are you out of luck? You would be, if you didn't have this ultra-cool TCA9548A 1-to-8 I2C multiplexer! Finally, a way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
  XT30 Connector male: Yellow XT60 connector for high current loads up to 40A female
  Fan - Ventilador: Ventilador de 2 pines, se encuentra comunmente en computadoras de escritorio
  JST connector male: jst connector
  JST connector female: jst connector
  push button: button 2 pin
  Lion Battery Pack 6s 3200mAh: Battery Holders Various common sizes : AA, AAA, 20mm coin cell and 12mm coin cell.
  Arduino_CNC_V3.00: Protoneer Arduino CNC Shield V3.00 If using Grbl V0.9: The “A” axis can not be used (yet). The “SCL” (Arduino A5) pin is now used for 'Probing' input. The “End Stops Z+ & Z-” (Arduino D11) and “SpnEn” (Arduino D12) have been switched!
  UBEC 5V6A: 2-6s input and 5v 6 A output ubec circuit
  XT30 Connector female: Yellow XT60 connector for high current loads up to 40A female
  Mini-360 DC-DC Buck converter: Mini-360 DC-DC Buck converter. Tiny buck step down voltage converter, input voltage 4.75 to 23V output 1 to 17V adjustable. Available from ebay and the like.
  INA219 DC Current Sensor Breakout: INA DC Current Sensor Breakout
  Adafruit APDS-9960: The APDS9960 from Avago Technologies has an integrated IR LED and driver, along with four directional photodiodes that sense reflected IR energy from the LED. It's proximity detection feature allows it to measure the distance an object is from the front of the sensor (up to a few centimeters) with 8 bit resolution. Since there are four IR sensors, you can measure the changes in light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
